# Fritzing sketch Ampare_monitor_1.0 (saved by Fritzing 0.9.8b)
breadboards: 1

parts:
  부품1 = Arduino Uno (Rev3)
  Grove1 = Grove OLED 128x96
  M1 = INA219 DC Current Monitor Module [part_number=CJMCU]
  M2 = INA219 DC Current Monitor Module [part_number=CJMCU]
  M3 = INA219 DC Current Monitor Module [part_number=CJMCU]
  LED1 = smd LED [color="Red (633nm)" package="1206 [SMD]"]
  LED2 = smd LED [color="Red (633nm)" package="1206 [SMD]"]
  R1 = Resistor [tolerance=±5% power=0.25 resistance=220 package=THT]
  R2 = Resistor [tolerance=±5% power=0.25 resistance=220 package=THT]
  M4 = 74HC4051 Module [part_number=WCMU-4051]

nets:
  N1: 부품1.A4/SDA, Grove1.SDA, M4.pin10, M4.pin15
  N2: 부품1.A5/SCL, Grove1.SCL, M1.SCL, M2.SCL, M3.SCL
  N3: 부품1.D5_PWM, M4.pin16
  N4: 부품1.D6_PWM, M4.pin17
  N5: 부품1.D7, M4.pin18
  N6: 부품1.5V, M1.Vin+
  N7: Grove1.GND, M4.pin19
  N8: Grove1.VCC, M3.Vin-
  VCC: M1.VCC, M1.Vin-, M2.VCC, M2.Vin+, M3.VCC, M3.Vin+, R2.Pin_1
  GND: M1.GND, M2.GND, M3.GND, LED1.anode, LED2.anode, M4.pin9, M4.pin11, M4.pin14
  N9: M1.SDA, M4.pin4
  N10: M2.SDA, M4.pin8
  N11: M2.Vin-, R1.Pin_1
  N12: M3.SDA, M4.pin7
  N13: LED1.cathode, R1.Pin_0
  N14: LED2.cathode, R2.Pin_0
  N15: M4.pin12, M4.pin13

custom parts:
  INA219 DC Current Monitor Module: INA219 DC Current Monitor Module Links: INA219 product information
  74HC4051 Module: 74HC4051 Analog Multiplexer Module Links: Nexperia website 74HC4051 Datasheet
