# Fritzing sketch Ampare_monitor_2.0 (saved by Fritzing 0.9.8b)
breadboards: 2

parts:
  M1 = INA219 DC Current Monitor Module [part_number=CJMCU]
  M2 = INA219 DC Current Monitor Module [part_number=CJMCU]
  M3 = 74HC4051 Module [part_number=WCMU-4051]
  Grove1 = Grove OLED 128x96
  부품1 = Arduino Uno (Rev3)
  LED2 = LED - 5mm [color="Yellow (595nm)" current=0.030 package="5 mm [THT]"]
  LED3 = LED - 5mm [color="Green (555nm)" current=0.030 package="5 mm [THT]"]
  LED4 = LED - 5mm [color="Red (633nm)" current=0.030 package="5 mm [THT]"]
  LED5 = LED - 5mm [color="Red (633nm)" current=0.030 package="5 mm [THT]"]
  LED6 = LED - 5mm [color="Red (633nm)" current=0.030 package="5 mm [THT]"]
  LED7 = LED - 5mm [color="Red (633nm)" current=0.030 package="5 mm [THT]"]
  LED8 = LED - 5mm [color="Red (633nm)" current=0.030 package="5 mm [THT]"]
  LED9 = LED - 5mm [color="Red (633nm)" current=0.030 package="5 mm [THT]"]
  R1 = Resistor [tolerance=±5% power=0.25 resistance=220 package=THT]
  R2 = Resistor [tolerance=±5% power=0.25 resistance=220 package=THT]
  R3 = Resistor [tolerance=±5% power=0.25 resistance=220 package=THT]
  LED10 = LED - 5mm [color="Red (633nm)" current=0.030 package="5 mm [THT]"]
  LED11 = LED - 5mm [color="Yellow (595nm)" current=0.030 package="5 mm [THT]"]
  LED12 = LED - 5mm [color="Green (555nm)" current=0.030 package="5 mm [THT]"]
  LED13 = LED - 5mm [color="Red (633nm)" current=0.030 package="5 mm [THT]"]
  R4 = Resistor [tolerance=±5% power=0.25 resistance=220 package=THT]
  R5 = Resistor [tolerance=±5% power=0.25 resistance=220 package=THT]
  R6 = Resistor [tolerance=±5% power=0.25 resistance=220 package=THT]
  R7 = Resistor [tolerance=±5% power=0.25 resistance=220 package=THT]
  R8 = Resistor [tolerance=±5% power=0.25 resistance=220 package=THT]
  R9 = Resistor [tolerance=±5% power=0.25 resistance=220 package=THT]
  R10 = Resistor [tolerance=±5% power=0.25 resistance=220 package=THT]
  R11 = Resistor [tolerance=±5% power=0.25 resistance=220 package=THT]
  R12 = Resistor [tolerance=±5% power=0.25 resistance=220 package=THT]
  S1 = Pushbutton [package="[THT]"]

nets:
  VCC: M1.VCC, M2.VCC, M2.Vin-, M3.pin10, M3.pin15, R7.Pin_1, R8.Pin_1, R9.Pin_1, R10.Pin_1, R12.Pin_1
  GND: M1.GND, M2.GND, M3.pin9, M3.pin11, M3.pin14, M3.pin19, Grove1.GND, 부품1.GND, 부품1.D2, LED2.cathode, LED3.cathode, LED4.cathode, LED5.cathode, LED6.cathode, LED7.cathode, LED8.cathode, LED9.cathode, LED10.cathode, LED11.cathode, LED13.cathode, R10.Pin_0, S1.Pin_1, S1.Pin_2
  N1: M1.SCL, M2.SCL, Grove1.SCL, 부품1.A5/SCL
  N2: M1.SDA, M3.pin8
  N3: M1.Vin-, Grove1.VCC, R11.Pin_1
  N4: M1.Vin+, 부품1.3V3
  N5: M2.SDA, M3.pin3
  N6: M2.Vin+, 부품1.5V
  N7: Grove1.SDA, 부품1.A4/SDA
  N8: 부품1.A0, R1.Pin_1
  N9: 부품1.A1, R2.Pin_1
  N10: 부품1.A2, R3.Pin_1
  N11: 부품1.A3, R6.Pin_1
  N12: 부품1.D4, R5.Pin_1
  N13: 부품1.D5_PWM, R4.Pin_1
  N14: LED2.anode, R2.Pin_0
  N15: LED3.anode, R1.Pin_0
  N16: LED4.anode, R7.Pin_0
  N17: LED5.anode, R8.Pin_0
  N18: LED6.anode, R9.Pin_0
  N19: LED8.anode, R11.Pin_0
  N20: LED9.anode, R12.Pin_0
  N21: R3.Pin_0, LED10.anode
  N22: LED11.anode, R5.Pin_0
  N23: LED12.anode, R6.Pin_0
  N24: LED13.anode, R4.Pin_0

notes:
  3.3v and gnd
  5V and gnd
  5V 부하용 LED 5 ea , 3.3v LED 1 ea
  5V 전류 경고등  3단계
  3.3V 전류 경고등  3단계

custom parts:
  INA219 DC Current Monitor Module: INA219 DC Current Monitor Module Links: INA219 product information
  74HC4051 Module: 74HC4051 Analog Multiplexer Module Links: Nexperia website 74HC4051 Datasheet
