# Fritzing sketch fan_control_breadboard_pinmap (saved by Fritzing 0.9.7b)
breadboards: 1

parts:
  Grove1 = Grove OLED 128x96
  RHT1 = Humidity and Temperature Sensor RHT03
  부품2 = Arduino Nano (Rev3.0)
  MD03A1 = Dual VNH2SP30 Motor Driver [part_number=MD03A]
  M1 = DC Motor
  M2 = DC Motor
  VCC1 = Battery block 9V

nets:
  GND: Grove1.GND, RHT1.GND_2, 부품2.GND
  VCC: Grove1.VCC, RHT1.Vcc, 부품2.5V
  N1: Grove1.SDA, 부품2.A4
  N2: Grove1.SCL, 부품2.A5
  N3: RHT1.Data-signal, 부품2.D12/MISO
  N4: 부품2.D3, MD03A1.1INa
  N5: 부품2.D4, MD03A1.1INb
  N6: 부품2.D5, MD03A1.PWM
  N7: 부품2.D6, MD03A1.2PWM
  N8: 부품2.D7, MD03A1.2INb#142
  N9: 부품2.D8, MD03A1.2INb#143
  N10: MD03A1.OUT_1A, M1.pin_1
  N11: MD03A1.OUT_1B, M1.pin_2
  N12: MD03A1.OUT_2A, M2.pin_1
  N13: MD03A1.OUT_2B, M2.pin_2
  N14: MD03A1.VIN, VCC1.+
  N15: MD03A1.GND, VCC1.-

notes:
  DHT22
  OLED 0.96'
  DC MOTOER < 1 >
  DC MOTOER < 2 >
  MOTOR DRIVER L298N GREENPCB
  12V미만 과 12V 이상은
  서로 다른 점퍼설정을 해야한다.
